# Fritzing sketch FinBit MSP432 Protoboard v1.0 (saved by Fritzing 0.9.3b)
circuit board: 8.46667cm x 5.64444cm
breadboards: 1

parts:
  Part1 = Adafruit PowerBoost 500 Shield [part_number="Adafruit #2078"]
  Part2 = Lithium Ion Polymer Battery 3.7v 500mAh [part_number=1578]
  Part3 = BME280 Breakout
  Part4 = Power Cell LiPo Charger/Booster  # not connected
  GY2 = MPU-6050 Board GY-521 [form="♀ (female)" package=THT]
  Launchpad1 = TI Launchpad MSP430G2
  SparkFun_Particle_Sensor_Breakout_-_MAX1 = SparkFun MAX30105_Breakout [part_number=SEN-14045]

nets:
  N1: Part1.VBAT, Part2.negative
  GND: Part1.GND, Part2.positive, Part3.GND, GY2.pin2, Launchpad1.p20, SparkFun_Particle_Sensor_Breakout_-_MAX1.GND
  3.3V: Part1.3V, Part3.3.3V, GY2.pin1, Launchpad1.p1, SparkFun_Particle_Sensor_Breakout_-_MAX1.5V
  N2: Part3.SDI/SDA, GY2.pin4, Launchpad1.p14, SparkFun_Particle_Sensor_Breakout_-_MAX1.SDA
  N3: Part3.SCK/SCL, GY2.pin3, Launchpad1.p15, SparkFun_Particle_Sensor_Breakout_-_MAX1.SCL

notes:
  This is similar to the MPU-9250 I'm using for the FinBit tag.
  I use the Arduino PowerBoost Shield to get clean 3v3 (blue wires) and 5v (red wires) power and to easily test the MSP432 using 100% battery power.
  Eventually I'll want to get us away from this to something like the board below + inductive charging.
  Note that nothing in this Fritz uses 5v, even though 5v is wired up for use. Some other sensors or devices might use 5v, so I'm keeping it around for awhile longer (e.g.: to power the MAX30105 green LED we need 5v power to drive maximum intensity).
  This is a stand-in for the MSP432, which has a lot more GPIO pins than the MSP430 (shown here).
  Fortunately Pins 1.6 and Pins 1.7 on both MSP430 and MSP432 boards are wired for I2C use, the communication standard I'm trying to adopt for all sensor package communication.
  Pin 1.6 carries SDA (data).
  Pin 1.7 carries SCL (clock).
  MAX30105 PulseOx Sensor Package
  Similar to BMP-280 pressure + temp sensor
  FinBit Prototype Design
  Dave Haas
  27 June 2017

custom parts:
  Adafruit PowerBoost 500 Shield: What's a project if it's trapped on your desk? Now you can take your Arduino anywhere you wish with the PowerBoost shield! This stackable shield goes onto your Arduino and provides a slim rechargeable power pack, with a built in battery charger as well as DC/DC booster. Compatible with Arduino Uno, Duemilanove, Mega, Leonardo and Due - basically any Arduino-pinout-shaped Arduino as only the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
  Lithium Ion Polymer Battery 3.7v 500mAh: Lithium ion polymer (also known as 'lipo' or 'lipoly') batteries are thin, light and powerful. The output ranges from 4.2V when completely charged to 3.7V. This battery has a capacity of 500mAh for a total of about 1.9 Wh. The batteries come pre-attached with a genuine 2-pin JST-PH connector as shown and include the necessary protection circuitry.
  MPU-6050 Board GY-521: Acelerometro y Giroscopio MPU-6050 Board GY-521
  SparkFun MAX30105_Breakout: Description: The SparkFun MAX30105 Particle Sensor is a flexible, powerful sensor enabling sensing of distance, heart rate, particle detection and even the blinking of an eye. The MAX30105 has been equipped with three LEDs as well as a very sensitive photon detector. The idea is to pulse the different LEDs, then detect what shines back. Based on the reflected signature it’s possible to detect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
